# Fritzing sketch Magic Lantern (saved by Fritzing 0.9.3b)
circuit board: 8.46667cm x 5.64444cm
breadboards: 1

parts:
  Part1 = 12 NeoPixel Ring [part_number=1643]
  Part2 = 12 NeoPixel Ring [part_number=1643]
  Part3 = Adafruit Feather HUZZAH ESP8266 [part_number="Adafruit #2821"]
  C1 = Electrolytic Capacitor [capacitance=0.1mF package="100 mil [THT, electrolytic]"]
  R1 = Resistor [tolerance=±5% resistance=330 package=THT]
  V1 = DC Power [voltage=5]

nets:
  N1: Part1.IN, Part2.OUT
  VDD: Part1.VDD, Part2.VDD, C1.+
  GND: Part1.GND, Part3.GND, C1.-, V1.V-
  N2: Part2.IN, R1.Pin_1
  N3: Part3.GPIO14/SCK, R1.Pin_0
  N4: Part3.VBUS, V1.V+

notes:
  VBUS = USB pin
  300-500 ohm

custom parts:
  12 NeoPixel Ring: 12 ultra bright smart LED NeoPixels are arranged in a circle with 1.5" (37mm) outer diameter. The rings are 'chainable' - connect the output pin of one to the input pin of another. Use only one microcontroller pin to control as many as you can chain together! Each LED is addressable as the driver chip is inside the LED. Each one has ~18mA constant current drive so the color will be very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
  Adafruit Feather HUZZAH ESP8266: his is the Adafruit Feather HUZZAH ESP8266 - our take on an 'all-in-one' ESP8266 WiFi development board with built in USB and battery charging. Its an ESP8266 WiFi module with all the extras you need, ready to rock! We have other boards in the Feather family, check'em out here. At the Feather HUZZAH's heart is an ESP8266 WiFi microcontroller clocked at 80 MHz and at 3.3V logic. This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
